# Fritzing sketch Exemplo_3 (saved by Fritzing 0.9.3b)
breadboards: 1

parts:
  Componente1 = Arduino Uno (Rev3)
  S1 = Pushbutton [package="[THT]"]
  R1 = Resistor [tolerance=±5% resistance=10k package=THT]
  LED1 = LED - 5mm [color="Yellow (592nm)" package="5 mm [THT]"]
  R2 = Resistor [tolerance=±5% resistance=330 package=THT]

nets:
  N1: Componente1.D13/SCK, LED1.anode
  N2: Componente1.D2, S1.Pin_3, S1.Pin_4, R1.Pin_1
  N3: Componente1.5V, S1.Pin_1, S1.Pin_2
  N4: Componente1.GND, R1.Pin_0, R2.Pin_0
  N5: LED1.cathode, R2.Pin_1
